# Fritzing sketch romi (saved by Fritzing 0.9.6b)
breadboards: 1

parts:
  PIC_left = PIC16F1705 [part_number=PIC16F1705 package="DIP (Dual Inline) [THT]"]
  PIC_right = PIC16F1705 [part_number=PIC16F1705 package="DIP (Dual Inline) [THT]"]  # not connected
  SDA = Resistor [tolerance=±5% resistance=10000 power=0.25 package=THT]
  MCLR_left = Resistor [tolerance=±5% resistance=10000 power=0.25 package=THT]
  led_left = Resistor [tolerance=±5% resistance=1k power=0.25 package=THT]
  MCLR_right = Resistor [tolerance=±5% resistance=10000 power=0.25 package=THT]  # not connected
  led_right = Resistor [tolerance=±5% resistance=1k power=0.25 package=THT]  # not connected
  LED_left = LED - 3mm [color="Red (633nm)" current=0.030 package="3 mm [THT]"]
  LED_right = LED - 3mm [color="Red (633nm)" current=0.030 package="3 mm [THT]"]  # not connected
  PWR_5v = Screw terminal - 2 pins [package=THT]
  U4 = PICKIT_3_PROG
  SCL = Resistor [tolerance=±5% resistance=10000 power=0.25 package=THT]
  RST = SWITCH-MOMENTARY-2 [package=tactile-pth]
  U5 = PICKIT_3_PROG  # not connected
  U6 = MOTOR_HEADER
  U7 = MOTOR_HEADER  # not connected
  I2C = Screw terminal - 2 pins [package=THT]

nets:
  VDD: PIC_left.Vdd, SDA.Pin_0, MCLR_left.Pin_0, PWR_5v.pin1, U4.VDD, SCL.Pin_0
  N1: PIC_left.RA5, U6.DIR
  N2: PIC_left.RA4, U6.PWM
  N3: PIC_left.MCLR/RA3, MCLR_left.Pin_1, U4.Vpp/MCLR, RST.2
  N4: PIC_left.RC5, U6.SLP
  N5: PIC_left.RC4, PIC_left.RC2, led_left.Pin_0, PWR_5v.pin2, U4.VSS, RST.1
  N6: PIC_left.RC3, LED_left.anode
  N7: PIC_left.Vss, SCL.Pin_1, I2C.pin1
  N8: PIC_left.RA0, SDA.Pin_1, I2C.pin2
  N9: PIC_left.RA1, U6.B
  N10: PIC_left.RA2, U6.A
  N11: PIC_left.RC0, U4.PGC
  N12: PIC_left.RC1, U4.PGD
  N13: led_left.Pin_1, LED_left.cathode

custom parts:
  PIC16F1705: Microchip PIC16F1705
  PICKIT_3_PROG: PICKIT 3 6-pin inline header
  MOTOR_HEADER: Header for motor driver
